# Fritzing sketch firmataDisplay (saved by Fritzing 0.9.2b)
breadboards: 1

parts:
  Bauteil1 = Arduino Uno (Rev3)
  LCD1 = LCD screen
  LED1 = LED - 5mm [color="Red (633nm)" package="5 mm [THT]"]
  LED2 = LED - 5mm [color="Yellow (585nm)" package="5 mm [THT]"]
  LED3 = LED - 5mm [color="Green (560nm)" package="5 mm [THT]"]
  LED4 = LED - 5mm [color="Blue (505nm)" package="5 mm [THT]"]
  R1 = Resistor [tolerance=±5% resistance=220 package=THT]
  R2 = Photocell (LDR) [package=THT]
  R3 = Rotary Potentiometer (Small) [maximum_resistance=100kΩ package=THT]
  R4 = Resistor [tolerance=±5% resistance=220 package=THT]

nets:
  N1: Bauteil1.A0, R1.Pin_1, R2.pin_0
  N2: Bauteil1.D8, LCD1.DB7
  N3: Bauteil1.D9_PWM, LCD1.DB6
  N4: Bauteil1.D10_PWM/SS, LCD1.DB5
  N5: Bauteil1.D11_PWM/MOSI, LCD1.DB4
  N6: Bauteil1.D12/MISO, LCD1.E
  N7: Bauteil1.D13/SCK, LCD1.RS
  GND: Bauteil1.GND, LCD1.VSS, LCD1.R/W, LCD1.LED-, LED1.cathode, LED2.cathode, LED3.cathode, LED4.cathode, R1.Pin_0, R3.leg1
  N8: Bauteil1.D2, LED1.anode
  N9: Bauteil1.D3_PWM, LED2.anode
  N10: Bauteil1.D4, LED3.anode
  N11: Bauteil1.D5_PWM, LED4.anode
  5V: Bauteil1.5V, LCD1.VDD, R2.pin_1, R3.leg2, R4.Pin_1
  N12: LCD1.V0, R3.wiper
  N13: LCD1.LED+, R4.Pin_0
